# Fritzing sketch Jetpong (saved by Fritzing 0.9.3b)
breadboards: 1

parts:
  DFRobot_Bluetooth_V1 = TEL0026-BluetoothV3
  元件2 = Arduino Nano (Rev3.0)
  BAT2 = BC9VPC [package=bc9vpc]
  RotationSensorDFR3 = RotationSensorDFR0058
  J8 = Dagu DGServo 9g header (male) [package=THT]
  J9 = Dagu DGServo 9g header (male) [package=THT]
  J10 = Basic Servo
  J11 = Dagu DGServo 9g header (male) [package=THT]
  J12 = Dagu DGServo 9g header (male) [package=THT]
  J13 = Basic Servo
  RotationSensorDFR4 = RotationSensorDFR0058
  S3 = Pushbutton [package="[THT]"]
  S4 = Pushbutton [package="[THT]"]
  R3 = Resistor [tolerance=±5% resistance=220 package="0402 [SMD]"]
  R4 = Resistor [tolerance=±5% resistance=220 package="0402 [SMD]"]

nets:
  N1: DFRobot_Bluetooth_V1.TXD, 元件2.D0/RX
  VCC: DFRobot_Bluetooth_V1.VCC, 元件2.5V, RotationSensorDFR3.5V, J8.Vcc, J9.Vcc, RotationSensorDFR4.5V, S3.Pin_2, S4.Pin_1, S4.Pin_2
  GND: DFRobot_Bluetooth_V1.GND, 元件2.GND, RotationSensorDFR3.GND, J8.pulse, J9.pulse, J10.gnd, J11.gnd, J12.gnd, J13.gnd, RotationSensorDFR4.GND, R3.Pin_0, R4.Pin_0
  N2: DFRobot_Bluetooth_V1.RXD, 元件2.D1/TX
  N3: 元件2.D10, J10.pulse, J12.pulse
  N4: 元件2.D11/MOSI, J11.pulse, J13.pulse
  VCC_2: 元件2.VIN, BAT2.V+, J10.vcc, J11.Vcc, J12.Vcc, J13.vcc
  N5: 元件2.A5, RotationSensorDFR3.SIGNAL, J9.gnd
  N6: 元件2.A4, J8.gnd, RotationSensorDFR4.SIGNAL
  N7: S3.Pin_3, S3.Pin_4, R4.Pin_1
  N8: S4.Pin_3, S4.Pin_4, R3.Pin_1

notes:
  下方 9V電池 (電壓供給伺服馬達)
  - 下方 紅線 9V
  - 下方 黑線 GND(與Arduino 共地)
  上方 Arduino 5V(電壓供給元件)
  - 上方 紅線 5V
  - 上方 黑線 GND
  伺服馬達 SG-5010
  - OUT(橙) 接 Arduino pin D10/D11(PWM)
  - VCC(紅) 接 9V
  - GND(黑) 接 Arduino pin GND
  YwRobotRotationSensor
  - OUT 接 Arduino pin A4/A5
  - VCC 接 Arduino pin 5V
  - GND 接 Arduino pin GND
  按鈕開關(建議電阻10K - 棕黑橙)
  - OUT 接 Arduino pin D2/D3
  - VCC 接 Arduino pin 5V
  - GND 接 Arduino pin 5V
  DFRobot-BluetoothV3
  - VCC 接 Arduino pin 5V
  - GND 接 Arduino pin GND
  - RXD 接 Arduino pin TXD
  - TXD 接 Arduino pin RXD
  燒錄時請先拔除RX, TX
